# Fritzing sketch Air quality sensor (saved by Fritzing 0.9.3b)

parts:
  WeMos_D1_Mini1 = WeMos D1 Mini
  Součástka1 = Adafruit CCS811
  Součástka2 = ws2812b [package="smd 2812b"]
  Grove1 = Grove OLED 128x96

nets:
  3V3: WeMos_D1_Mini1.3V3, Součástka1.VIN
  5V: WeMos_D1_Mini1.5V, Součástka2.VDD, Grove1.VCC
  N1: WeMos_D1_Mini1.D1, Součástka1.SCL, Grove1.SCL
  N2: WeMos_D1_Mini1.D2, Součástka1.SDA, Grove1.SDA
  N3: WeMos_D1_Mini1.D7, Součástka2.DIN
  GND: WeMos_D1_Mini1.G, Součástka1.GND, Součástka1.!WAKE, Součástka2.VSS, Grove1.GND
